# Fritzing sketch FlowerBase (saved by Fritzing 1.0.1rc)
breadboards: 1

parts:
  A1 = Particle - Photon2
  OLED_I2C1 = OLED 128x64 I2C Monochrome Display

nets:
  3.3V: A1.Pin_2, OLED_I2C1.VDD
  GND: A1.Pin_4, OLED_I2C1.GND
  N1: A1.Pin_17, OLED_I2C1.SDA
  N2: A1.Pin_18, OLED_I2C1.SCK
  5V: A1.Pin_28, A1.Pin_29

custom parts:
  Particle - Photon2: The Photon 2 is a microcontroller and Wi-Fi networking developed by particle. Features: 802.11a/b/g/n Wi-Fi, 2.4 GHz and 5 GHz Integrated PCB antenna Integrated U.FL connector for external antenna Integrated RF switch BLE 5 using same antenna as Wi-Fi Realtek RTL8721DM MCU ARM Cortex M33 CPU, 200 MHz 2048 KB (2 MB) user application maximum size 3072 KB (3 MB) of RAM available to user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
